# Fritzing sketch fritzingSchema (saved by Fritzing 0.8.3b)
perfboards: 1

parts:
  R1 = Resistor [tolerance=±5% resistance=10k package=THT]
  R2 = Resistor [tolerance=±5% resistance=10k package=THT]
  R3 = Resistor [tolerance=±5% resistance=10k package=THT]
  R4 = Resistor [tolerance=±5% resistance=10k package=THT]
  S2 = SWITCH-MOMENTARY-2 [package=tactile-switch-1101ne]
  S3 = SWITCH-MOMENTARY-2 [package=tactile-switch-1101ne]
  S4 = SWITCH-MOMENTARY-2 [package=tactile-switch-1101ne]
  S5 = SWITCH-MOMENTARY-2 [package=tactile-switch-1101ne]
  Part1 = Arduino Uno (Rev3)

nets:
  N1: R1.Pin_1, S2.1, Part1.D4
  N2: R2.Pin_1, S3.1, Part1.D5_PWM
  N3: R3.Pin_0, R4.Pin_0
  N4: R3.Pin_1, S4.1, Part1.D6_PWM
  N5: R4.Pin_1, S5.1, Part1.D7
  N6: S2.2, S3.2, S4.2, S5.2, Part1.5V
